# Fritzing sketch photomaton (saved by Fritzing 0.9.3b)
breadboards: 1

parts:
  Raspberry_Pi_1 = Raspberry Pi 3 [part_number=RPI-3-V1.2]
  S1 = Pushbutton [package="[THT]"]
  S2 = Pushbutton [package="[THT]"]

nets:
  N1: Raspberry_Pi_1.GPIO2, S2.Pin_1, S2.Pin_2
  N2: Raspberry_Pi_1.GND, S1.Pin_3, S1.Pin_4, S2.Pin_3
  N3: S1.Pin_1, S1.Pin_2

notes:
  GND droit à l'image
  vers GND écran
  vers 5V écran
  GPIO 2 droit à l'image
  GND pas droit à l'image
  GPIO 3 droit à l'image
